// Logisim project SiPU.circ as structural Verilog: 23 circuits, main circuit main
module main (
  input  Download_ROM,
  input  in_2,
  input  _0,
  input  _1,
  input  _2,
  input  _3,
  input  _4,
  input  _5,
  input  _6,
  input  _7,
  input  _8,
  input  _9,
  output out_13
);

  wire adder_1_out_3, and_1_out, and_2_out, and_3_out, and_5_out, bcd_screen_1_out_3, bcd_screen_1_out_4,
       bcd_screen_1_out_5, bcd_screen_1_out_6, bcd_screen_1_out_7, bcd_screen_1_out_8, bcd_screen_1_out_9,
       bcd_screen_1_out_10, bcd_screen_1_out_11, bcd_screen_1_out_12, bcd_screen_1_out_13,
       bcd_screen_1_out_14, bcd_screen_1_out_15, bcd_screen_1_out_16, bcd_screen_1_out_17,
       bcd_screen_1_out_18, bcd_screen_1_out_19, bcd_screen_1_out_20, bcd_screen_1_out_21,
       bcd_screen_1_out_22, bcd_screen_1_out_23, cu_1_a_receive, cu_1_a_transmit, cu_1_alu_add_sub,
       cu_1_ar_receive, cu_1_ar_transmit, cu_1_control_input, cu_1_control_pc_a, cu_1_control_print,
       cu_1_dr_receive, cu_1_dr_transmit, cu_1_ir_receive, cu_1_ir_transmit, cu_1_l_receive, cu_1_l_transmit,
       cu_1_mar_receive, cu_1_mar_transmit, cu_1_mbr_receive, cu_1_mbr_transmit, cu_1_out_5, cu_1_pc_receive,
       cu_1_pc_transmit, cu_1_r0_receive, cu_1_r0_transmit, cu_1_r1_receive, cu_1_r1_transmit,
       cu_1_r_receive, cu_1_r_transmit, not_1_out, not_2_out, not_3_out, not_4_out, or_2_out, or_3_out,
       or_4_out, or_5_out, or_7_out, or_8_out, rom_1_out_6, rom_1_receive, rom_1_receive_2, rom_1_transmit,
       rom_1_transmit_2;
  wire [2:0] alu_1_out_4;
  wire [7:0] adder_1_out_2, alu_1_out_5, and_4_out, input_buffer_1_out_4, n1_1_8_1_out_3, or_1_out, or_6_out,
       or_9_out, or_10_out, or_11_out, or_12_out, pc_address_1_out_5, ram_1_out_9, register_1_out_5,
       register_2_out_5, register_3_out_5, register_4_out_5, register_5_out_5, register_6_out_5,
       register_7_out_5, register_8_out_5, register_9_out_5, register_10_out_5, rom_1_out_4, rom_1_out_5;

  not not_1 (not_1_out, and_5_out);
  and and_1 (and_1_out, Download_ROM, not_1_out);
  ROM rom_1 (
    .out_4(rom_1_out_4), .out_5(rom_1_out_5), .Transmit(rom_1_transmit), .Transmit_2(rom_1_transmit_2),
    .out_6(rom_1_out_6), .in_1(and_1_out), .receive_2(rom_1_receive_2), .receive(rom_1_receive),
    .out_9(out_13));
  and and_2 (and_2_out, not_2_out, cu_1_control_print);
  not not_2 (not_2_out, and_3_out);
  register register_1 (
    .in_2(1'b1), .in_4(or_9_out), .out_5(register_1_out_5), .enable_receiving(and_2_out), .ON_OFF(and_5_out));
  BCD__screen bcd_screen_1 (
    .out_15(bcd_screen_1_out_15), .out_16(bcd_screen_1_out_16), .out_17(bcd_screen_1_out_17),
    .out_18(bcd_screen_1_out_18), .out_19(bcd_screen_1_out_19), .out_20(bcd_screen_1_out_20),
    .out_21(bcd_screen_1_out_21), .out_22(bcd_screen_1_out_22), .out_23(bcd_screen_1_out_23),
    .out_3(bcd_screen_1_out_3), .out_4(bcd_screen_1_out_4), .out_5(bcd_screen_1_out_5),
    .out_6(bcd_screen_1_out_6), .out_7(bcd_screen_1_out_7), .out_8(bcd_screen_1_out_8),
    .out_9(bcd_screen_1_out_9), .out_10(bcd_screen_1_out_10), .out_11(bcd_screen_1_out_11),
    .out_12(bcd_screen_1_out_12), .out_13(bcd_screen_1_out_13), .in_2(register_1_out_5), .in_1(1'b1),
    .out_14(bcd_screen_1_out_14));
  assign or_1_out = or_9_out | rom_1_out_5;  // OR_Gate or_1, 8 bits wide
  or or_2 (or_2_out, rom_1_transmit_2, cu_1_dr_transmit);
  or or_3 (or_3_out, cu_1_dr_receive, rom_1_receive_2);
  or or_4 (or_4_out, rom_1_transmit, cu_1_ar_transmit);
  or or_5 (or_5_out, cu_1_ar_receive, rom_1_receive);
  assign or_6_out = or_9_out | rom_1_out_4;  // OR_Gate or_6, 8 bits wide
  or or_7 (or_7_out, cu_1_out_5, rom_1_out_6);
  and and_3 (and_3_out, _0, Download_ROM);
  or or_8 (or_8_out, and_5_out, Download_ROM);
  Input_Buffer input_buffer_1 (
    .out_4(input_buffer_1_out_4), .Buffer_Transmit(cu_1_control_input),
    .in_3({_9, _8, _7, _6, _5, _4, _3, _2, _1, _0}), .ON_OFF(and_5_out));
  _7_Segment_Display u_7_segment_display_1 (
    .g(bcd_screen_1_out_3), .f(bcd_screen_1_out_4), .a(bcd_screen_1_out_5), .b(bcd_screen_1_out_6),
    .e(bcd_screen_1_out_15), .d(bcd_screen_1_out_16), .c(bcd_screen_1_out_17));  // open: dp
  RAM ram_1 (
    .in_1(or_1_out), .transmit_DR(or_2_out), .DR_receive(or_3_out), .CU_AR(or_5_out), .R_W(or_7_out),
    .out_9(ram_1_out_9), .in_6(or_6_out), .in_5(or_4_out), .ON_OFF(or_8_out));
  _7_Segment_Display u_7_segment_display_2 (
    .g(bcd_screen_1_out_7), .f(bcd_screen_1_out_8), .a(bcd_screen_1_out_9), .b(bcd_screen_1_out_10),
    .e(bcd_screen_1_out_18), .d(bcd_screen_1_out_19), .c(bcd_screen_1_out_20));  // open: dp
  assign or_9_out = ram_1_out_9 | and_4_out | register_3_out_5 | register_2_out_5 | input_buffer_1_out_4;  // OR_Gate or_9, 8 bits wide
  _7_Segment_Display u_7_segment_display_3 (
    .g(bcd_screen_1_out_11), .f(bcd_screen_1_out_12), .a(bcd_screen_1_out_13), .b(bcd_screen_1_out_14),
    .e(bcd_screen_1_out_21), .d(bcd_screen_1_out_22), .c(bcd_screen_1_out_23));  // open: dp
  assign or_10_out = or_12_out | or_9_out;  // OR_Gate or_10, 8 bits wide
  assign or_11_out = register_6_out_5 | or_9_out;  // OR_Gate or_11, 8 bits wide
  assign or_12_out = register_4_out_5 | register_3_out_5 | register_10_out_5 | register_5_out_5;  // OR_Gate or_12, 8 bits wide
  register register_2 (
    .in_2(cu_1_mar_transmit), .in_4(or_11_out), .out_5(register_2_out_5),
    .enable_receiving(cu_1_mar_receive), .ON_OFF(and_5_out));
  register register_3 (
    .in_2(cu_1_mbr_transmit), .in_4(or_10_out), .out_5(register_3_out_5),
    .enable_receiving(cu_1_mbr_receive), .ON_OFF(and_5_out));
  register register_4 (
    .in_2(cu_1_r0_transmit), .in_4(or_12_out), .out_5(register_4_out_5), .enable_receiving(cu_1_r0_receive),
    .ON_OFF(and_5_out));
  register register_5 (
    .in_2(cu_1_r1_transmit), .in_4(or_12_out), .out_5(register_5_out_5), .enable_receiving(cu_1_r1_receive),
    .ON_OFF(and_5_out));
  PC_address pc_address_1 (
    .in_3(adder_1_out_2), .IR(and_4_out), .out_5(pc_address_1_out_5), .CU(cu_1_control_pc_a), .in_2(and_5_out));
  register register_6 (
    .in_2(cu_1_pc_transmit), .in_4(pc_address_1_out_5), .out_5(register_6_out_5),
    .enable_receiving(cu_1_pc_receive), .ON_OFF(and_5_out));
  register register_7 (
    .in_2(cu_1_l_transmit), .in_4(or_12_out), .out_5(register_7_out_5), .enable_receiving(cu_1_l_receive),
    .ON_OFF(and_5_out));
  register register_8 (
    .in_2(cu_1_r_transmit), .in_4(or_12_out), .out_5(register_8_out_5), .enable_receiving(cu_1_r_receive),
    .ON_OFF(and_5_out));
  _1_1__8 u_1_1_8_1 (.in_1(cu_1_ir_transmit), .out_3(n1_1_8_1_out_3), .in_2(cu_1_ir_transmit));
  register register_9 (
    .in_2(1'b1), .in_4(register_3_out_5), .out_5(register_9_out_5), .enable_receiving(cu_1_ir_receive),
    .ON_OFF(and_5_out));
  CU cu_1 (
    .in_2(register_9_out_5), .Control_PC_A(cu_1_control_pc_a), .out_5(cu_1_out_5),
    .DR_receive(cu_1_dr_receive), .DR_transmit(cu_1_dr_transmit), .AR_receive(cu_1_ar_receive),
    .AR_transmit(cu_1_ar_transmit), .MAR_receive(cu_1_mar_receive), .MAR_transmit(cu_1_mar_transmit),
    .MBR_receive(cu_1_mbr_receive), .MBR_transmit(cu_1_mbr_transmit), .R0_receive(cu_1_r0_receive),
    .R0_transmit(cu_1_r0_transmit), .R1_receive(cu_1_r1_receive), .R1_transmit(cu_1_r1_transmit),
    .L_receive(cu_1_l_receive), .STATUS_FROM_ALU(alu_1_out_4), .L_transmit(cu_1_l_transmit),
    .R_receive(cu_1_r_receive), .R_transmit(cu_1_r_transmit), .A_receive(cu_1_a_receive),
    .A_transmit(cu_1_a_transmit), .PC_receive(cu_1_pc_receive), .PC_transmit(cu_1_pc_transmit),
    .IR_receive(cu_1_ir_receive), .IR_transmit(cu_1_ir_transmit), .ALU_Add_Sub(cu_1_alu_add_sub),
    .Control_Input(cu_1_control_input), .Control_Print(cu_1_control_print), .ON_OFF(and_5_out));  // open: RAM_receive, RAM_transmit
  ALU alu_1 (
    .ADD___SUB(cu_1_alu_add_sub), .R_Reg(register_8_out_5), .L_Reg(register_7_out_5), .out_5(alu_1_out_5),
    .out_4(alu_1_out_4));
  Adder adder_1 (.in_1(register_6_out_5), .out_2(adder_1_out_2), .out_3(adder_1_out_3));
  assign and_4_out = n1_1_8_1_out_3 & register_9_out_5;  // AND_Gate and_4, 8 bits wide
  register register_10 (
    .in_2(cu_1_a_transmit), .in_4(alu_1_out_5), .out_5(register_10_out_5), .enable_receiving(cu_1_a_receive),
    .ON_OFF(and_5_out));
  not not_3 (not_3_out, adder_1_out_3);
  not not_4 (not_4_out, and_3_out);
  and and_5 (and_5_out, in_2, not_3_out, not_4_out);

  // Notes on the sheet:
  //   If 1, ROM is done
  //   Keypad
  //   Display
  //   if (input = 0 AND Multiplying)
  //   SYSTEM BUS
  //   MAR
  //   MBR
  //   R0
  //   R1
  //   CPU BUS
  //   PC
  //   ALU L
  //   ALU R
  //   ADDER
  //   IR
  //   0 = OFF     1 = ON
  //   POWER BUTTON
endmodule

module register (
  input  enable_receiving,
  input  in_2,
  input  ON_OFF,
  input  [7:0] in_4,
  output [7:0] out_5
);

  wire clock_1_out, not_1_out, or_1_out;
  wire [7:0] d_ff_8_q, or_2_out;

  or or_1 (or_1_out, enable_receiving, not_1_out);
  not not_1 (not_1_out, ON_OFF);
  assign or_2_out = in_4;  // OR_Gate or_2, 8 bits wide OR_Gate
  Clock clock_1 (.out(clock_1_out));
  D_Flip_Flop d_ff_1 (.clk(clock_1_out), .D(or_2_out[7]), .Q(d_ff_8_q[7]), .en(or_1_out));  // open: Qn, preset, reset
  D_Flip_Flop d_ff_2 (.clk(clock_1_out), .D(or_2_out[6]), .Q(d_ff_8_q[6]), .en(or_1_out));  // open: Qn, preset, reset
  D_Flip_Flop d_ff_3 (.clk(clock_1_out), .D(or_2_out[5]), .Q(d_ff_8_q[5]), .en(or_1_out));  // open: Qn, preset, reset
  D_Flip_Flop d_ff_4 (.clk(clock_1_out), .D(or_2_out[4]), .Q(d_ff_8_q[4]), .en(or_1_out));  // open: Qn, preset, reset
  D_Flip_Flop d_ff_5 (.clk(clock_1_out), .D(or_2_out[3]), .Q(d_ff_8_q[3]), .en(or_1_out));  // open: Qn, preset, reset
  D_Flip_Flop d_ff_6 (.clk(clock_1_out), .D(or_2_out[2]), .Q(d_ff_8_q[2]), .en(or_1_out));  // open: Qn, preset, reset
  D_Flip_Flop d_ff_7 (.clk(clock_1_out), .D(or_2_out[1]), .Q(d_ff_8_q[1]), .en(or_1_out));  // open: Qn, preset, reset
  D_Flip_Flop d_ff_8 (.clk(clock_1_out), .D(or_2_out[0]), .Q(d_ff_8_q[0]), .en(or_1_out));  // open: Qn, preset, reset
  assign out_5 = {8{in_2}} & d_ff_8_q;  // AND_Gate and_1, 8 bits wide

  // Notes on the sheet:
  //   enable transmitting
endmodule

module Adder (
  input  [7:0] in_1,
  output [7:0] out_2,
  output out_3
);

  wire or_1_out, undriven;
  wire [7:0] and_1_out, not_1_out;

  Adder_part adder_1 (.a(in_1), .b(8'h1), .out(out_2));  // open: cin, cout
  assign not_1_out = ~8'hf;  // NOT_Gate not_1, 8 bits wide
  assign and_1_out = out_2 & not_1_out;  // AND_Gate and_1, 8 bits wide
  Clock clock_1 ();  // open: out
  or or_1 (or_1_out, and_1_out[0], and_1_out[1], and_1_out[2], and_1_out[3], and_1_out[4], and_1_out[5], and_1_out[6], and_1_out[7]);
  J_K_Flip_Flop j_k_ff_1 (.J(or_1_out), .clk(undriven), .Q(out_3));  // open: K, Qn, preset, en, reset
endmodule

module _2_8__1 (
  input  [7:0] in_1,
  input  [7:0] in_2,
  output out_3
);

  wire [7:0] and_1_out, and_2_out, not_1_out, not_2_out, or_1_out;

  assign not_1_out = ~in_1;  // NOT_Gate not_1, 8 bits wide
  assign not_2_out = ~in_2;  // NOT_Gate not_2, 8 bits wide
  assign and_1_out = not_1_out & not_2_out;  // AND_Gate and_1, 8 bits wide
  assign and_2_out = in_1 & in_2;  // AND_Gate and_2, 8 bits wide
  assign or_1_out = and_1_out | and_2_out;  // OR_Gate or_1, 8 bits wide
  and and_3 (out_3, or_1_out[0], or_1_out[1], or_1_out[2], or_1_out[3], or_1_out[5], or_1_out[6], or_1_out[7], or_1_out[4]);
endmodule

module RAM (
  input  [7:0] in_1,
  input  transmit_DR,
  input  DR_receive,
  input  CU_AR,
  input  in_5,
  input  [7:0] in_6,
  input  ON_OFF,
  input  R_W,
  output [7:0] out_9
);

  wire and_1_out, and_2_out, and_3_out, and_4_out, and_5_out, and_6_out, and_7_out, and_8_out, and_9_out,
       and_10_out, and_11_out, and_12_out, and_13_out, and_14_out, and_15_out, and_16_out, and_17_out,
       and_18_out, and_19_out, and_20_out, and_21_out, and_22_out, and_23_out, and_24_out, and_25_out,
       and_26_out, and_27_out, and_28_out, and_29_out, and_30_out, and_31_out, and_32_out, n2_8_1_1_out_3,
       n2_8_1_2_out_3, n2_8_1_3_out_3, n2_8_1_4_out_3, n2_8_1_5_out_3, n2_8_1_6_out_3, n2_8_1_7_out_3,
       n2_8_1_8_out_3, n2_8_1_9_out_3, n2_8_1_10_out_3, n2_8_1_11_out_3, n2_8_1_12_out_3, n2_8_1_13_out_3,
       n2_8_1_14_out_3, n2_8_1_15_out_3, n2_8_1_16_out_3, not_1_out, not_2_out;
  wire [7:0] or_1_out, or_2_out, register_1_out_5, register_2_out_5, register_3_out_5, register_4_out_5,
       register_5_out_5, register_6_out_5, register_7_out_5, register_8_out_5, register_9_out_5,
       register_10_out_5, register_11_out_5, register_12_out_5, register_13_out_5, register_14_out_5,
       register_15_out_5, register_16_out_5, register_17_out_5;

  register register_1 (
    .in_2(in_5), .in_4({4'b0000, in_6[3:0]}), .out_5(register_1_out_5), .enable_receiving(CU_AR),
    .ON_OFF(ON_OFF));
  _2_8__1 u_2_8_1_1 (.in_1(register_1_out_5), .in_2(8'hf), .out_3(n2_8_1_1_out_3));
  _2_8__1 u_2_8_1_2 (.in_1(register_1_out_5), .in_2(8'he), .out_3(n2_8_1_2_out_3));
  _2_8__1 u_2_8_1_3 (.in_1(register_1_out_5), .in_2(8'hd), .out_3(n2_8_1_3_out_3));
  _2_8__1 u_2_8_1_4 (.in_1(register_1_out_5), .in_2(8'hc), .out_3(n2_8_1_4_out_3));
  _2_8__1 u_2_8_1_5 (.in_1(register_1_out_5), .in_2(8'hb), .out_3(n2_8_1_5_out_3));
  _2_8__1 u_2_8_1_6 (.in_1(register_1_out_5), .in_2(8'ha), .out_3(n2_8_1_6_out_3));
  _2_8__1 u_2_8_1_7 (.in_1(register_1_out_5), .in_2(8'h9), .out_3(n2_8_1_7_out_3));
  _2_8__1 u_2_8_1_8 (.in_1(register_1_out_5), .in_2(8'h8), .out_3(n2_8_1_8_out_3));
  _2_8__1 u_2_8_1_9 (.in_1(register_1_out_5), .in_2(8'h7), .out_3(n2_8_1_9_out_3));
  _2_8__1 u_2_8_1_10 (.in_1(register_1_out_5), .in_2(8'h6), .out_3(n2_8_1_10_out_3));
  _2_8__1 u_2_8_1_11 (.in_1(register_1_out_5), .in_2(8'h5), .out_3(n2_8_1_11_out_3));
  _2_8__1 u_2_8_1_12 (.in_1(register_1_out_5), .in_2(8'h4), .out_3(n2_8_1_12_out_3));
  _2_8__1 u_2_8_1_13 (.in_1(register_1_out_5), .in_2(8'h3), .out_3(n2_8_1_13_out_3));
  _2_8__1 u_2_8_1_14 (.in_1(register_1_out_5), .in_2(8'h2), .out_3(n2_8_1_14_out_3));
  _2_8__1 u_2_8_1_15 (.in_1(register_1_out_5), .in_2(8'h1), .out_3(n2_8_1_15_out_3));
  _2_8__1 u_2_8_1_16 (.in_1(register_1_out_5), .in_2({8{1'b0}}), .out_3(n2_8_1_16_out_3));
  not not_1 (not_1_out, R_W);
  and and_1 (and_1_out, n2_8_1_1_out_3, not_1_out);
  and and_2 (and_2_out, n2_8_1_2_out_3, not_1_out);
  and and_3 (and_3_out, n2_8_1_3_out_3, not_1_out);
  and and_4 (and_4_out, n2_8_1_4_out_3, not_1_out);
  and and_5 (and_5_out, n2_8_1_5_out_3, not_1_out);
  and and_6 (and_6_out, n2_8_1_6_out_3, not_1_out);
  and and_7 (and_7_out, n2_8_1_7_out_3, not_1_out);
  and and_8 (and_8_out, n2_8_1_8_out_3, not_1_out);
  and and_9 (and_9_out, n2_8_1_9_out_3, not_1_out);
  and and_10 (and_10_out, n2_8_1_10_out_3, not_1_out);
  and and_11 (and_11_out, n2_8_1_11_out_3, not_1_out);
  and and_12 (and_12_out, n2_8_1_12_out_3, not_1_out);
  and and_13 (and_13_out, n2_8_1_13_out_3, not_1_out);
  and and_14 (and_14_out, n2_8_1_14_out_3, not_1_out);
  and and_15 (and_15_out, n2_8_1_15_out_3, not_1_out);
  and and_16 (and_16_out, n2_8_1_16_out_3, not_1_out);
  and and_17 (and_17_out, n2_8_1_1_out_3, in_5, not_2_out);
  and and_18 (and_18_out, n2_8_1_2_out_3, in_5, not_2_out);
  and and_19 (and_19_out, n2_8_1_3_out_3, in_5, not_2_out);
  and and_20 (and_20_out, n2_8_1_4_out_3, in_5, not_2_out);
  and and_21 (and_21_out, n2_8_1_5_out_3, in_5, not_2_out);
  and and_22 (and_22_out, n2_8_1_6_out_3, in_5, not_2_out);
  and and_23 (and_23_out, n2_8_1_7_out_3, in_5, not_2_out);
  and and_24 (and_24_out, n2_8_1_8_out_3, in_5, not_2_out);
  and and_25 (and_25_out, n2_8_1_9_out_3, in_5, not_2_out);
  and and_26 (and_26_out, n2_8_1_10_out_3, in_5, not_2_out);
  and and_27 (and_27_out, n2_8_1_11_out_3, in_5, not_2_out);
  and and_28 (and_28_out, n2_8_1_12_out_3, in_5, not_2_out);
  and and_29 (and_29_out, n2_8_1_13_out_3, in_5, not_2_out);
  and and_30 (and_30_out, n2_8_1_14_out_3, in_5, not_2_out);
  and and_31 (and_31_out, n2_8_1_15_out_3, in_5, not_2_out);
  and and_32 (and_32_out, n2_8_1_16_out_3, in_5, not_2_out);
  not not_2 (not_2_out, not_1_out);
  register register_2 (
    .in_2(and_1_out), .in_4(out_9), .out_5(register_2_out_5), .enable_receiving(and_17_out), .ON_OFF(ON_OFF));
  register register_3 (
    .in_2(and_2_out), .in_4(out_9), .out_5(register_3_out_5), .enable_receiving(and_18_out), .ON_OFF(ON_OFF));
  register register_4 (
    .in_2(and_3_out), .in_4(out_9), .out_5(register_4_out_5), .enable_receiving(and_19_out), .ON_OFF(ON_OFF));
  register register_5 (
    .in_2(and_4_out), .in_4(out_9), .out_5(register_5_out_5), .enable_receiving(and_20_out), .ON_OFF(ON_OFF));
  register register_6 (
    .in_2(and_5_out), .in_4(out_9), .out_5(register_6_out_5), .enable_receiving(and_21_out), .ON_OFF(ON_OFF));
  register register_7 (
    .in_2(and_6_out), .in_4(out_9), .out_5(register_7_out_5), .enable_receiving(and_22_out), .ON_OFF(ON_OFF));
  register register_8 (
    .in_2(and_7_out), .in_4(out_9), .out_5(register_8_out_5), .enable_receiving(and_23_out), .ON_OFF(ON_OFF));
  register register_9 (
    .in_2(and_8_out), .in_4(out_9), .out_5(register_9_out_5), .enable_receiving(and_24_out), .ON_OFF(ON_OFF));
  register register_10 (
    .in_2(and_9_out), .in_4(out_9), .out_5(register_10_out_5), .enable_receiving(and_25_out), .ON_OFF(ON_OFF));
  register register_11 (
    .in_2(and_10_out), .in_4(out_9), .out_5(register_11_out_5), .enable_receiving(and_26_out), .ON_OFF(ON_OFF));
  register register_12 (
    .in_2(and_11_out), .in_4(out_9), .out_5(register_12_out_5), .enable_receiving(and_27_out), .ON_OFF(ON_OFF));
  register register_13 (
    .in_2(and_12_out), .in_4(out_9), .out_5(register_13_out_5), .enable_receiving(and_28_out), .ON_OFF(ON_OFF));
  register register_14 (
    .in_2(and_13_out), .in_4(out_9), .out_5(register_14_out_5), .enable_receiving(and_29_out), .ON_OFF(ON_OFF));
  register register_15 (
    .in_2(and_14_out), .in_4(out_9), .out_5(register_15_out_5), .enable_receiving(and_30_out), .ON_OFF(ON_OFF));
  register register_16 (
    .in_2(and_15_out), .in_4(out_9), .out_5(register_16_out_5), .enable_receiving(and_31_out), .ON_OFF(ON_OFF));
  register register_17 (
    .in_2(and_16_out), .in_4(out_9), .out_5(register_17_out_5), .enable_receiving(and_32_out), .ON_OFF(ON_OFF));
  assign or_1_out = register_2_out_5 | register_3_out_5 | register_4_out_5 | register_5_out_5 | register_6_out_5 | register_7_out_5 | register_8_out_5 | register_9_out_5 | register_10_out_5 | register_11_out_5 | register_12_out_5 | register_13_out_5 | register_14_out_5 | register_15_out_5 | register_16_out_5 | register_17_out_5;  // OR_Gate or_1, 8 bits wide
  assign or_2_out = in_1 | or_1_out;  // OR_Gate or_2, 8 bits wide
  register register_18 (
    .in_2(transmit_DR), .in_4(or_2_out), .out_5(out_9), .enable_receiving(DR_receive), .ON_OFF(ON_OFF));

  // Notes on the sheet:
  //   AR
  //   0=R 1=W
  //   Input from CPU Reg
  //   DR
endmodule

module _1_1__8 (
  input  in_1,
  input  in_2,
  output [7:0] out_3
);

  assign out_3 = {8{in_1}} & {8{in_2}};  // AND_Gate and_1, 8 bits wide
endmodule

module ALU (
  input  ADD___SUB,
  input  [7:0] R_Reg,
  input  [7:0] L_Reg,
  output [2:0] out_4,
  output [7:0] out_5
);

  wire adder_2_cout, and_1_out, and_2_out, and_3_out, and_4_out, and_8_out, not_1_out, not_2_out, not_3_out,
       not_4_out, not_5_out, not_6_out, not_7_out;
  wire [7:0] adder_1_out, adder_2_out, and_5_out, and_6_out, n2s_complement_machine_1_out_2, not_8_out;
  wire [7:7] decoder_1_out0, decoder_1_out1;

  Decoder decoder_1 (.out0(decoder_1_out0[7]), .out1(decoder_1_out1[7]), .sel(ADD___SUB));  // open: en
  Adder_part adder_1 (.a(R_Reg), .b(L_Reg), .out(adder_1_out));  // open: cin, cout
  _2s_complement_machine u_2s_complement_machine_1 (.in_1(L_Reg), .out_2(n2s_complement_machine_1_out_2));
  not not_1 (not_1_out, R_Reg[7]);
  not not_2 (not_2_out, L_Reg[7]);
  not not_3 (not_3_out, L_Reg[7]);
  not not_4 (not_4_out, out_5[7]);
  not not_5 (not_5_out, out_5[7]);
  not not_6 (not_6_out, L_Reg[7]);
  Adder_part adder_2 (
    .a(n2s_complement_machine_1_out_2), .b(R_Reg), .out(adder_2_out), .cout(adder_2_cout));  // open: cin
  and and_1 (and_1_out, decoder_1_out0[7], not_1_out, not_2_out, out_5[7]);
  and and_2 (and_2_out, decoder_1_out0[7], not_3_out, R_Reg[7], out_5[7]);
  and and_3 (and_3_out, decoder_1_out1[7], R_Reg[7], L_Reg[7], not_4_out);
  and and_4 (and_4_out, not_5_out, not_6_out, decoder_1_out1[7], R_Reg[7]);
  assign and_5_out = {8{decoder_1_out0[7]}} & adder_1_out;  // AND_Gate and_5, 8 bits wide
  assign and_6_out = {8{decoder_1_out1[7]}} & adder_2_out;  // AND_Gate and_6, 8 bits wide
  not not_7 (not_7_out, adder_2_cout);
  assign out_5 = and_5_out | and_6_out;  // OR_Gate or_1, 8 bits wide
  and and_7 (out_4[2], decoder_1_out1[7], not_7_out);
  or or_2 (out_4[1], and_1_out, and_2_out, and_3_out, and_4_out);
  assign not_8_out = ~out_5;  // NOT_Gate not_8, 8 bits wide
  and and_8 (and_8_out, not_8_out[0], not_8_out[1], not_8_out[2], not_8_out[3], not_8_out[5], not_8_out[6], not_8_out[7], not_8_out[4]);
  and and_9 (out_4[0], decoder_1_out1[7], and_8_out);

  // Notes on the sheet:
  //   R +- L
  //   Add
  //   Substract
  //   negative
  //   overflow
  //   0 = not overflow
  //   1 = overflow
  //   negative
  //   0 = +
  //   1 = -1
  //   1 - L,R are equal
  //   0 = L,R not equal
  //   equality
  //   STATUS
  //   negative     overflow      equal
endmodule

module _2s_complement_machine (
  input  [7:0] in_1,
  output [7:0] out_2
);

  wire [7:0] not_1_out;

  assign not_1_out = ~in_1;  // NOT_Gate not_1, 8 bits wide
  Adder_part adder_1 (.a(not_1_out), .b({8{1'b0}}), .out(out_2), .cin(1'b1));  // open: cout
endmodule

module CU (
  input  ON_OFF,
  input  [7:0] in_2,
  input  [2:0] STATUS_FROM_ALU,
  output Control_PC_A,
  output out_5,
  output DR_receive,
  output DR_transmit,
  output AR_receive,
  output AR_transmit,
  output MAR_receive,
  output MAR_transmit,
  output MBR_receive,
  output MBR_transmit,
  output R0_receive,
  output R0_transmit,
  output R1_receive,
  output R1_transmit,
  output L_receive,
  output L_transmit,
  output R_receive,
  output R_transmit,
  output A_receive,
  output A_transmit,
  output PC_receive,
  output PC_transmit,
  output IR_receive,
  output IR_transmit,
  output RAM_receive,
  output RAM_transmit,
  output ALU_Add_Sub,
  output Control_Input,
  output Control_Print
);

  wire and_1_out, and_2_out, and_3_out, demultiplexer_1_out0, demultiplexer_1_out1, demultiplexer_1_out2,
       demultiplexer_1_out3, not_1_out, or_1_out;
  wire [31:0] init_cpu_1_out_2, n01_1_out_4, n10_1_out_4, n11_1_out_5;
  wire [31:1] or_2_out;

  not not_1 (not_1_out, ON_OFF);
  Demultiplexer #(.select(2)) demultiplexer_1 (
    .out0(demultiplexer_1_out0), .out1(demultiplexer_1_out1), .out2(demultiplexer_1_out2),
    .out3(demultiplexer_1_out3), .in(1'b1), .sel(in_2[7:6]));  // open: en
  _00 u_00_1 (.in_1(or_1_out), .in_2(in_2));
  or or_1 (or_1_out, demultiplexer_1_out0, not_1_out);
  and and_1 (and_1_out, demultiplexer_1_out1, ON_OFF);
  _01 u_01_1 (.in_1(and_1_out), .in_2(in_2), .out_4(n01_1_out_4), .in_3(ON_OFF));
  and and_2 (and_2_out, demultiplexer_1_out2, ON_OFF);
  _10 u_10_1 (.in_1(and_2_out), .in_2(in_2), .out_4(n10_1_out_4), .in_3(ON_OFF));
  and and_3 (and_3_out, demultiplexer_1_out3, ON_OFF);
  _11 u_11_1 (.in_1(and_3_out), .in_2(in_2), .out_5(n11_1_out_5), .in_3(STATUS_FROM_ALU[0]), .in_4(ON_OFF));
  Init_CPU init_cpu_1 (.in_1(ON_OFF), .out_2(init_cpu_1_out_2));
  assign {or_2_out[31:30], Control_Print, Control_Input, ALU_Add_Sub, RAM_transmit, RAM_receive, IR_transmit, IR_receive, PC_transmit, PC_receive, A_transmit, A_receive, R_transmit, R_receive, L_transmit, L_receive, R1_transmit, R1_receive, R0_transmit, R0_receive, MBR_transmit, MBR_receive, MAR_transmit, MAR_receive, AR_transmit, AR_receive, DR_transmit, DR_receive, out_5, or_2_out[1], Control_PC_A} = init_cpu_1_out_2 | n01_1_out_4 | n10_1_out_4 | n11_1_out_5;  // OR_Gate or_2, 32 bits wide

  // Notes on the sheet:
  //   0 = Add, 1 = IR
endmodule

module PC_address (
  input  CU,
  input  in_2,
  input  [7:0] in_3,
  input  [7:0] IR,
  output [7:0] out_5
);

  wire [7:0] and_1_out, and_2_out;
  wire [7:7] demultiplexer_1_out0, demultiplexer_1_out1;

  Demultiplexer demultiplexer_1 (
    .out0(demultiplexer_1_out0[7]), .out1(demultiplexer_1_out1[7]), .in(1'b1), .sel(CU));  // open: en
  assign and_1_out = {8{demultiplexer_1_out0[7]}} & in_3 & {8{in_2}};  // AND_Gate and_1, 8 bits wide
  assign and_2_out = {8{demultiplexer_1_out1[7]}} & {4'b0000, IR[3:0]} & {8{in_2}};  // AND_Gate and_2, 8 bits wide
  assign out_5 = and_1_out | and_2_out;  // OR_Gate or_1, 8 bits wide

  // Notes on the sheet:
  //   Adder
endmodule

module MAR_A (
  input  CU,
  input  [7:0] in_2,
  input  [7:0] in_3,
  output [7:0] out_4
);

  wire [7:0] and_1_out, and_2_out;

  assign and_1_out = {8{CU}} & in_2;  // AND_Gate and_1, 8 bits wide
  assign and_2_out = in_3 & in_2;  // AND_Gate and_2, 8 bits wide
  assign out_4 = and_1_out | and_2_out;  // OR_Gate or_1, 8 bits wide

  // Notes on the sheet:
  //   0 = PC, 1 = RAM
  //   PC
  //   RAM
endmodule

module MBR_Data (
  input  CU,
  input  [7:0] CPU_Reg,
  input  [7:0] RAM,
  output [7:0] out_4
);

  wire [7:0] and_1_out, and_2_out;

  assign and_1_out = {8{CU}} & CPU_Reg;  // AND_Gate and_1, 8 bits wide
  assign and_2_out = RAM & CPU_Reg;  // AND_Gate and_2, 8 bits wide
  assign out_4 = and_1_out | and_2_out;  // OR_Gate or_1, 8 bits wide

  // Notes on the sheet:
  //   0 = CPU reg, 1 = RAM
endmodule

module _01 (
  input  in_1,
  input  [7:0] in_2,
  input  in_3,
  output [31:0] out_4
);

  wire and_1_out, and_2_out, and_3_out, and_4_out, and_5_out, and_6_out, and_7_out, and_8_out, and_9_out,
       and_10_out, and_11_out, and_12_out, and_13_out, and_14_out, and_15_out, and_16_out, and_17_out,
       and_18_out, and_19_out, and_20_out, and_21_out, and_22_out, and_23_out, and_24_out, and_25_out,
       and_26_out, and_27_out, and_28_out, and_29_out, and_30_out, clock_1_out, clock_2_out, clock_3_out,
       d_ff_1_q, d_ff_2_q, d_ff_3_q, d_ff_4_q, d_ff_5_q, d_ff_6_q, j_k_ff_1_q, j_k_ff_1_qn, not_1_out,
       not_2_out, not_3_out, not_4_out, not_5_out, not_6_out, not_7_out, not_8_out, not_9_out, not_10_out,
       not_11_out, not_12_out, not_13_out, not_14_out, not_15_out, not_16_out, not_17_out, not_18_out,
       not_19_out, not_20_out, not_21_out, not_23_out, not_24_out, not_25_out, not_26_out, not_27_out,
       not_28_out, not_29_out, not_30_out, not_31_out, or_1_out, or_2_out;

  not not_1 (not_1_out, in_1);
  or or_1 (or_1_out, not_1_out, j_k_ff_1_q);
  not not_2 (not_2_out, in_2[5]);
  Clock clock_1 (.out(clock_1_out));
  and and_1 (and_1_out, in_1, in_2[5]);
  and and_2 (and_2_out, in_1, not_2_out);
  D_Flip_Flop d_ff_1 (.clk(clock_1_out), .D(not_3_out), .Q(d_ff_1_q), .preset(or_1_out));  // open: Qn, en, reset
  D_Flip_Flop d_ff_2 (.clk(d_ff_1_q), .D(not_4_out), .Q(d_ff_2_q), .preset(or_1_out));  // open: Qn, en, reset
  D_Flip_Flop d_ff_3 (.clk(d_ff_2_q), .D(not_5_out), .Q(d_ff_3_q), .preset(or_1_out));  // open: Qn, en, reset
  not not_3 (not_3_out, d_ff_1_q);
  not not_4 (not_4_out, d_ff_2_q);
  not not_5 (not_5_out, d_ff_3_q);
  not not_6 (not_6_out, not_4_out);
  not not_7 (not_7_out, not_5_out);
  not not_8 (not_8_out, not_3_out);
  not not_9 (not_9_out, not_5_out);
  not not_10 (not_10_out, not_5_out);
  not not_11 (not_11_out, not_3_out);
  not not_12 (not_12_out, not_4_out);
  not not_13 (not_13_out, not_4_out);
  not not_14 (not_14_out, not_3_out);
  not not_15 (not_15_out, or_1_out);
  and and_3 (and_3_out, not_3_out, not_6_out, not_7_out);
  and and_4 (and_4_out, and_2_out, and_3_out);
  and and_5 (and_5_out, not_8_out, not_4_out, not_9_out);
  and and_6 (and_6_out, and_5_out, and_2_out);
  and and_7 (and_7_out, not_3_out, not_4_out, not_10_out);
  and and_8 (and_8_out, not_11_out, not_12_out, not_5_out);
  and and_9 (and_9_out, not_3_out, not_13_out, not_5_out);
  not not_16 (not_16_out, in_2[4]);
  and and_10 (and_10_out, not_14_out, not_4_out, not_5_out);
  Clock clock_2 (.out(clock_2_out));
  or or_2 (or_2_out, not_17_out, and_30_out);
  not not_17 (not_17_out, in_3);
  not not_18 (not_18_out, in_2[4]);
  and and_11 (and_11_out, and_5_out, and_1_out);
  and and_12 (and_12_out, and_7_out, and_1_out);
  and and_13 (and_13_out, and_7_out, and_2_out);
  and and_14 (and_14_out, and_8_out, and_1_out);
  and and_15 (and_15_out, and_8_out, and_2_out);
  and and_16 (and_16_out, and_9_out, and_1_out);
  and and_17 (and_17_out, and_9_out, and_2_out);
  J_K_Flip_Flop j_k_ff_1 (
    .J(and_10_out), .clk(clock_2_out), .K(or_2_out), .Q(j_k_ff_1_q), .Qn(j_k_ff_1_qn));  // open: preset, en, reset
  and and_18 (and_18_out, and_1_out, and_3_out, in_2[4]);
  and and_19 (and_19_out, not_18_out, and_3_out, and_1_out);
  and and_20 (and_20_out, and_17_out, in_2[4]);
  and and_21 (and_21_out, and_17_out, not_16_out);
  Clock clock_3 (.out(clock_3_out));
  and and_22 (and_22_out, and_3_out, and_1_out);
  D_Flip_Flop d_ff_4 (.clk(clock_3_out), .D(not_19_out), .Q(d_ff_4_q), .preset(j_k_ff_1_qn));  // open: Qn, en, reset
  D_Flip_Flop d_ff_5 (.clk(d_ff_4_q), .D(not_20_out), .Q(d_ff_5_q), .preset(j_k_ff_1_qn));  // open: Qn, en, reset
  D_Flip_Flop d_ff_6 (.clk(d_ff_5_q), .D(not_21_out), .Q(d_ff_6_q), .preset(j_k_ff_1_qn));  // open: Qn, en, reset
  not not_19 (not_19_out, d_ff_4_q);
  not not_20 (not_20_out, d_ff_5_q);
  not not_21 (not_21_out, d_ff_6_q);
  and and_23 (and_23_out, in_1, not_15_out, and_1_out);
  // NOT_Gate not_22 has open pins: in=j_k_ff_1_qn, out=open
  not not_23 (not_23_out, not_20_out);
  not not_24 (not_24_out, not_21_out);
  not not_25 (not_25_out, not_19_out);
  not not_26 (not_26_out, not_21_out);
  not not_27 (not_27_out, not_21_out);
  not not_28 (not_28_out, not_19_out);
  not not_29 (not_29_out, not_20_out);
  not not_30 (not_30_out, not_20_out);
  not not_31 (not_31_out, not_19_out);
  and and_24 (and_24_out, not_19_out, not_23_out, not_24_out);
  and and_25 (and_25_out, not_25_out, not_20_out, not_26_out);
  and and_26 (and_26_out, not_19_out, not_20_out, not_27_out);
  and and_27 (and_27_out, not_28_out, not_29_out, not_21_out);
  and and_28 (and_28_out, not_19_out, not_30_out, not_21_out);
  and and_29 (and_29_out, not_31_out, not_20_out, not_21_out);
  and and_30 (and_30_out, not_19_out, not_20_out, not_21_out);
  buf or_3 (out_4[0], 1'b0);  // OR_Gate
  buf or_4 (out_4[1], 1'b0);  // OR_Gate
  buf or_5 (out_4[2], and_23_out);  // OR_Gate
  or or_6 (out_4[3], and_11_out, and_27_out, and_13_out);
  or or_7 (out_4[4], and_16_out, and_28_out, and_15_out);
  or or_8 (out_4[5], and_14_out, and_26_out, and_6_out);
  or or_9 (out_4[6], and_16_out, and_27_out, and_13_out);
  or or_10 (out_4[7], and_12_out, and_25_out, and_4_out);
  or or_11 (out_4[8], and_14_out, and_26_out, and_6_out);
  or or_12 (out_4[9], and_22_out, and_28_out, and_15_out);
  or or_13 (out_4[10], and_11_out, and_29_out, and_17_out);
  buf or_14 (out_4[11], and_21_out);  // OR_Gate
  buf or_15 (out_4[12], and_19_out);  // OR_Gate
  buf or_16 (out_4[13], and_20_out);  // OR_Gate
  buf or_17 (out_4[14], and_18_out);  // OR_Gate
  buf or_18 (out_4[15], 1'b0);  // OR_Gate
  buf or_19 (out_4[16], 1'b0);  // OR_Gate
  buf or_20 (out_4[17], 1'b0);  // OR_Gate
  buf or_21 (out_4[18], 1'b0);  // OR_Gate
  buf or_22 (out_4[19], 1'b0);  // OR_Gate
  buf or_23 (out_4[20], 1'b0);  // OR_Gate
  or or_24 (out_4[21], 1'b0, and_24_out);
  or or_25 (out_4[22], 1'b0, and_25_out, and_24_out);
  or or_26 (out_4[23], 1'b0, and_29_out);
  or or_27 (out_4[24], and_12_out, and_4_out);
  or or_28 (out_4[25], and_16_out, and_13_out);
  buf or_29 (out_4[26], 1'b0);  // OR_Gate

  assign out_4[31:27] = {5{1'b0}};

  // Notes on the sheet:
  //   010 = Load
  //   011 = Save
  //   if 3
  //   if 1
  //   if 1 and load
  //   if 2
  //   if 4
  //   if 5
  //   R1
  //   R0
  //   if 6
  //   if load
  //   r0/r1
  //   if save
  //   if load
  //   if save
  //   if load
  //   if save
  //   if save
  //   if 1
  //   if 2
  //   3
  //   4
  //   5
  //   6
  //   7
  //   0
  //   3
  //   14
  //   18
  //   22
  //   8
  //   10
  //   25
endmodule

module _10 (
  input  in_1,
  input  [7:0] in_2,
  input  in_3,
  output [31:0] out_4
);

  wire and_1_out, and_2_out, and_3_out, and_4_out, and_5_out, and_6_out, and_7_out, and_8_out, and_9_out,
       and_10_out, and_11_out, and_12_out, and_13_out, and_14_out, and_15_out, and_16_out, and_17_out,
       and_18_out, and_19_out, and_20_out, and_21_out, and_22_out, and_23_out, and_24_out, and_25_out,
       and_26_out, and_27_out, and_28_out, and_29_out, and_30_out, and_31_out, and_32_out, and_33_out,
       and_34_out, and_35_out, clock_1_out, clock_2_out, clock_3_out, d_ff_1_q, d_ff_2_q, d_ff_3_q, d_ff_4_q,
       d_ff_5_q, d_ff_6_q, j_k_ff_1_q, j_k_ff_1_qn, not_1_out, not_2_out, not_3_out, not_4_out, not_5_out,
       not_6_out, not_7_out, not_8_out, not_9_out, not_10_out, not_11_out, not_12_out, not_13_out,
       not_14_out, not_15_out, not_16_out, not_17_out, not_18_out, not_19_out, not_20_out, not_21_out,
       not_22_out, not_23_out, not_25_out, not_26_out, not_27_out, not_28_out, not_29_out, not_30_out,
       not_31_out, not_32_out, not_33_out, or_1_out, or_2_out, or_3_out, or_4_out, or_5_out, or_6_out,
       or_7_out;

  not not_1 (not_1_out, in_1);
  not not_2 (not_2_out, in_2[5]);
  Clock clock_1 (.out(clock_1_out));
  or or_1 (or_1_out, not_1_out, j_k_ff_1_q);
  and and_1 (and_1_out, in_1, not_2_out);
  and and_2 (and_2_out, in_1, in_2[5]);
  not not_3 (not_3_out, in_2[4]);
  D_Flip_Flop d_ff_1 (.clk(clock_1_out), .D(not_4_out), .Q(d_ff_1_q), .preset(or_1_out));  // open: Qn, en, reset
  D_Flip_Flop d_ff_2 (.clk(d_ff_1_q), .D(not_5_out), .Q(d_ff_2_q), .preset(or_1_out));  // open: Qn, en, reset
  D_Flip_Flop d_ff_3 (.clk(d_ff_2_q), .D(not_6_out), .Q(d_ff_3_q), .preset(or_1_out));  // open: Qn, en, reset
  and and_3 (and_3_out, and_2_out, not_3_out);
  and and_4 (and_4_out, and_2_out, in_2[4]);
  not not_4 (not_4_out, d_ff_1_q);
  not not_5 (not_5_out, d_ff_2_q);
  not not_6 (not_6_out, d_ff_3_q);
  and and_5 (and_5_out, and_10_out, and_2_out);
  not not_7 (not_7_out, not_5_out);
  not not_8 (not_8_out, not_6_out);
  not not_9 (not_9_out, not_4_out);
  not not_10 (not_10_out, not_6_out);
  not not_11 (not_11_out, in_2[3]);
  not not_12 (not_12_out, not_6_out);
  not not_13 (not_13_out, not_4_out);
  not not_14 (not_14_out, not_5_out);
  not not_15 (not_15_out, not_5_out);
  and and_6 (and_6_out, and_10_out, and_4_out);
  and and_7 (and_7_out, and_3_out, and_9_out);
  and and_8 (and_8_out, and_9_out, and_4_out);
  and and_9 (and_9_out, not_4_out, not_7_out, not_8_out);
  and and_10 (and_10_out, not_9_out, not_5_out, not_10_out);
  and and_11 (and_11_out, and_10_out, and_3_out, in_2[3]);
  and and_12 (and_12_out, not_11_out, and_3_out, and_10_out);
  and and_13 (and_13_out, not_4_out, not_5_out, not_12_out);
  and and_14 (and_14_out, not_13_out, not_14_out, not_6_out);
  and and_15 (and_15_out, not_4_out, not_15_out, not_6_out);
  Clock clock_2 (.out(clock_2_out));
  not not_16 (not_16_out, in_3);
  not not_17 (not_17_out, in_2[3]);
  not not_18 (not_18_out, in_2[3]);
  and and_16 (and_16_out, and_10_out, and_1_out);
  and and_17 (and_17_out, and_13_out, and_1_out);
  and and_18 (and_18_out, and_14_out, and_1_out);
  and and_19 (and_19_out, and_15_out, and_1_out);
  or or_2 (or_2_out, and_5_out, and_19_out);
  J_K_Flip_Flop j_k_ff_1 (
    .J(or_2_out), .clk(clock_2_out), .K(or_3_out), .Q(j_k_ff_1_q), .Qn(j_k_ff_1_qn));  // open: preset, en, reset
  or or_3 (or_3_out, not_16_out, and_35_out);
  and and_20 (and_20_out, and_1_out, and_9_out, in_2[3]);
  and and_21 (and_21_out, not_17_out, and_9_out, and_1_out);
  and and_22 (and_22_out, and_16_out, not_18_out);
  and and_23 (and_23_out, and_1_out, in_2[3], and_16_out);
  or or_4 (or_4_out, and_11_out, and_12_out);
  not not_19 (not_19_out, in_2[3]);
  Clock clock_3 (.out(clock_3_out));
  not not_20 (not_20_out, in_2[3]);
  and and_24 (and_24_out, and_8_out, and_4_out, in_2[3]);
  and and_25 (and_25_out, not_19_out, and_4_out, and_8_out);
  D_Flip_Flop d_ff_4 (.clk(clock_3_out), .D(not_21_out), .Q(d_ff_4_q), .preset(j_k_ff_1_qn));  // open: Qn, en, reset
  D_Flip_Flop d_ff_5 (.clk(d_ff_4_q), .D(not_22_out), .Q(d_ff_5_q), .preset(j_k_ff_1_qn));  // open: Qn, en, reset
  D_Flip_Flop d_ff_6 (.clk(d_ff_5_q), .D(not_23_out), .Q(d_ff_6_q), .preset(j_k_ff_1_qn));  // open: Qn, en, reset
  and and_26 (and_26_out, and_1_out, and_18_out, in_2[3]);
  and and_27 (and_27_out, not_20_out, and_18_out, and_1_out);
  not not_21 (not_21_out, d_ff_4_q);
  not not_22 (not_22_out, d_ff_5_q);
  not not_23 (not_23_out, d_ff_6_q);
  or or_5 (or_5_out, and_20_out, and_22_out, and_24_out);
  or or_6 (or_6_out, and_21_out, and_23_out, and_25_out);
  // NOT_Gate not_24 has open pins: in=j_k_ff_1_qn, out=open
  or or_7 (or_7_out, and_7_out, and_8_out);
  not not_25 (not_25_out, not_22_out);
  not not_26 (not_26_out, not_23_out);
  not not_27 (not_27_out, not_21_out);
  not not_28 (not_28_out, not_23_out);
  not not_29 (not_29_out, not_23_out);
  not not_30 (not_30_out, not_21_out);
  not not_31 (not_31_out, not_22_out);
  not not_32 (not_32_out, not_22_out);
  not not_33 (not_33_out, not_21_out);
  and and_28 (and_28_out, and_9_out, and_1_out);
  and and_29 (and_29_out, not_21_out, not_25_out, not_26_out);
  and and_30 (and_30_out, not_27_out, not_22_out, not_28_out);
  and and_31 (and_31_out, not_21_out, not_22_out, not_29_out);
  and and_32 (and_32_out, not_30_out, not_31_out, not_23_out);
  and and_33 (and_33_out, not_21_out, not_32_out, not_23_out);
  and and_34 (and_34_out, not_33_out, not_22_out, not_23_out);
  and and_35 (and_35_out, not_21_out, not_22_out, not_23_out);
  buf or_8 (out_4[0], 1'b0);  // OR_Gate
  buf or_9 (out_4[1], 1'b0);  // OR_Gate
  buf or_10 (out_4[2], 1'b0);  // OR_Gate
  buf or_11 (out_4[3], and_32_out);  // OR_Gate
  buf or_12 (out_4[4], and_33_out);  // OR_Gate
  buf or_13 (out_4[5], and_31_out);  // OR_Gate
  buf or_14 (out_4[6], and_32_out);  // OR_Gate
  buf or_15 (out_4[7], and_30_out);  // OR_Gate
  buf or_16 (out_4[8], and_31_out);  // OR_Gate
  or or_17 (out_4[9], and_33_out, or_7_out);
  or or_18 (out_4[10], or_4_out, and_34_out, and_6_out);
  or or_19 (out_4[11], and_27_out, and_12_out);
  buf or_20 (out_4[12], or_6_out);  // OR_Gate
  or or_21 (out_4[13], and_26_out, and_11_out);
  buf or_22 (out_4[14], or_5_out);  // OR_Gate
  buf or_23 (out_4[15], and_16_out);  // OR_Gate
  buf or_24 (out_4[16], and_17_out);  // OR_Gate
  buf or_25 (out_4[17], and_28_out);  // OR_Gate
  buf or_26 (out_4[18], and_17_out);  // OR_Gate
  buf or_27 (out_4[19], and_17_out);  // OR_Gate
  buf or_28 (out_4[20], and_18_out);  // OR_Gate
  buf or_29 (out_4[21], and_29_out);  // OR_Gate
  or or_30 (out_4[22], and_29_out, and_30_out);
  or or_31 (out_4[23], and_34_out, 1'b0);
  buf or_32 (out_4[24], 1'b0);  // OR_Gate
  buf or_33 (out_4[25], 1'b0);  // OR_Gate
  buf or_34 (out_4[26], 1'b0);  // OR_Gate
  buf or_35 (out_4[27], in_2[4]);  // OR_Gate
  buf or_36 (out_4[28], and_7_out);  // OR_Gate
  buf or_37 (out_4[29], and_6_out);  // OR_Gate

  assign out_4[31:30] = 2'b00;

  // Notes on the sheet:
  //   1000 = ADD
  //   1001 = SUBTRACT
  //   1010 = INPUT
  //   1011 = PRINT
  //   R1/R2
  //   INPUT
  //   PRINT
  //   ALU Add/Subtract
  //   End INPUT/PRINT
  //   if ADD/SUBTRACT
  //   if INPUT/PRINT
  //   INPUT
  //   if 2
  //   PRINT
  //   if 1
  //   if 1
  //   if 1
  //   if 2
  //   if 3
  //   if 4
  //   if 5
  //   INPUT
  //   PRINT
  //   PRINT
  //   R2
  //   R1
  //   R2
  //   R1
  //   R2
  //   R1
  //   20 & R1/R2
  //   End ADD/SUBTRACT
  //   13
  //   11
  //   16-18-19
  //   R2
  //   R1
  //   Next Instruction
  //   R2
  //   R1
  //   13
  //   11
  //   17
  //   14
  //   12
  //   10
  //   if 1
  //   if 2
  //   3
  //   4
  //   5
  //   6
  //   7
  //   11
  //   12
  //   0
  //   1
  //   2
  //   3
  //   4
  //   5
  //   6
  //   7
  //   8
  //   9
  //   10
  //   13
  //   14
  //   15
  //   16
  //   17
  //   18
  //   19
  //   20
  //   21
  //   22
  //   23
  //   24
  //   25
  //   26
  //   27
  //   28
  //   29
endmodule

module _00 (
  input  in_1,
  input  [7:0] in_2
);
endmodule

module _11 (
  input  in_1,
  input  [7:0] in_2,
  input  in_3,
  input  in_4,
  output [31:0] out_5
);

  wire and_1_out, and_2_out, and_3_out, and_4_out, and_5_out, and_6_out, and_7_out, and_8_out, and_9_out,
       and_10_out, and_11_out, and_12_out, and_13_out, and_14_out, and_15_out, and_21_out, clock_1_out,
       clock_2_out, clock_3_out, d_ff_1_q, d_ff_2_q, d_ff_3_q, d_ff_4_q, d_ff_5_q, d_ff_6_q, d_ff_7_q,
       j_k_ff_1_q, j_k_ff_1_qn, not_1_out, not_2_out, not_3_out, not_4_out, not_5_out, not_6_out, not_7_out,
       not_8_out, not_9_out, not_10_out, not_11_out, not_12_out, not_13_out, not_14_out, not_15_out,
       not_16_out, not_17_out, not_18_out, not_19_out, not_20_out, not_21_out, not_22_out, not_23_out,
       not_24_out, not_25_out, not_26_out, not_27_out, not_28_out, not_29_out, not_30_out, or_1_out,
       or_2_out, or_3_out, or_4_out;

  Clock clock_1 (.out(clock_1_out));
  not not_1 (not_1_out, in_1);
  or or_1 (or_1_out, not_1_out, j_k_ff_1_q);
  and and_1 (and_1_out, clock_1_out, out_5[27]);
  D_Flip_Flop #(.trigger("falling")) d_ff_1 (.clk(and_1_out), .D(in_3), .Q(d_ff_1_q));  // open: Qn, preset, en, reset
  D_Flip_Flop d_ff_2 (.clk(clock_1_out), .D(not_2_out), .Q(d_ff_2_q), .preset(or_1_out));  // open: Qn, en, reset
  D_Flip_Flop d_ff_3 (.clk(d_ff_2_q), .D(not_3_out), .Q(d_ff_3_q), .preset(or_1_out));  // open: Qn, en, reset
  D_Flip_Flop d_ff_4 (.clk(d_ff_3_q), .D(not_4_out), .Q(d_ff_4_q), .preset(or_1_out));  // open: Qn, en, reset
  not not_2 (not_2_out, d_ff_2_q);
  not not_3 (not_3_out, d_ff_3_q);
  not not_4 (not_4_out, d_ff_4_q);
  not not_5 (not_5_out, not_3_out);
  not not_6 (not_6_out, not_4_out);
  not not_7 (not_7_out, not_2_out);
  not not_8 (not_8_out, not_4_out);
  not not_9 (not_9_out, not_4_out);
  not not_10 (not_10_out, not_2_out);
  not not_11 (not_11_out, not_3_out);
  not not_12 (not_12_out, not_3_out);
  and and_2 (and_2_out, not_2_out, not_5_out, not_6_out);
  and and_3 (and_3_out, not_7_out, not_3_out, not_8_out);
  and and_4 (and_4_out, not_2_out, not_3_out, not_9_out);
  and and_5 (and_5_out, not_10_out, not_11_out, not_4_out);
  and and_6 (and_6_out, not_2_out, not_12_out, not_4_out);
  Clock clock_2 (.out(clock_2_out));
  or or_2 (or_2_out, not_13_out, and_21_out);
  not not_13 (not_13_out, in_4);
  not not_14 (not_14_out, in_2[5]);
  J_K_Flip_Flop j_k_ff_1 (
    .J(and_6_out), .clk(clock_2_out), .K(or_2_out), .Q(j_k_ff_1_q), .Qn(j_k_ff_1_qn));  // open: preset, en, reset
  buf and_7 (and_7_out, in_2[5]);  // AND_Gate
  buf and_8 (and_8_out, not_14_out);  // AND_Gate
  Clock clock_3 (.out(clock_3_out));
  D_Flip_Flop d_ff_5 (.clk(clock_3_out), .D(not_15_out), .Q(d_ff_5_q), .preset(j_k_ff_1_qn));  // open: Qn, en, reset
  D_Flip_Flop d_ff_6 (.clk(d_ff_5_q), .D(not_16_out), .Q(d_ff_6_q), .preset(j_k_ff_1_qn));  // open: Qn, en, reset
  D_Flip_Flop d_ff_7 (.clk(d_ff_6_q), .D(not_17_out), .Q(d_ff_7_q), .preset(j_k_ff_1_qn));  // open: Qn, en, reset
  or or_3 (or_3_out, and_7_out, and_8_out);
  not not_15 (not_15_out, d_ff_5_q);
  not not_16 (not_16_out, d_ff_6_q);
  not not_17 (not_17_out, d_ff_7_q);
  and and_9 (and_9_out, and_2_out, or_3_out);
  and and_10 (and_10_out, and_3_out, or_3_out);
  and and_11 (and_11_out, or_3_out, and_4_out);
  and and_12 (and_12_out, and_8_out, d_ff_1_q, and_5_out);
  and and_13 (and_13_out, and_7_out, not_18_out, and_5_out);
  not not_18 (not_18_out, d_ff_1_q);
  and and_14 (and_14_out, and_5_out, not_19_out, and_8_out);
  not not_19 (not_19_out, and_12_out);
  not not_20 (not_20_out, and_13_out);
  and and_15 (and_15_out, and_5_out, not_20_out, and_7_out);
  not not_21 (not_21_out, j_k_ff_1_qn);
  not not_22 (not_22_out, not_16_out);
  not not_23 (not_23_out, not_17_out);
  not not_24 (not_24_out, not_15_out);
  not not_25 (not_25_out, not_17_out);
  not not_26 (not_26_out, not_17_out);
  not not_27 (not_27_out, not_15_out);
  not not_28 (not_28_out, not_16_out);
  not not_29 (not_29_out, not_16_out);
  not not_30 (not_30_out, not_15_out);
  or or_4 (or_4_out, and_14_out, and_15_out);
  and and_16 (out_5[7], not_15_out, not_22_out, not_23_out);
  and and_17 (out_5[8], not_24_out, not_16_out, not_25_out);
  and and_18 (out_5[6], not_15_out, not_16_out, not_26_out);
  and and_19 (out_5[9], not_27_out, not_28_out, not_17_out);
  and and_20 (out_5[23], not_15_out, not_29_out, not_17_out);
  and and_21 (and_21_out, not_30_out, not_16_out, not_17_out);
  or or_5 (out_5[0], and_13_out, and_12_out);
  buf or_6 (out_5[12], and_9_out);  // OR_Gate
  buf or_7 (out_5[14], and_10_out);  // OR_Gate
  buf or_8 (out_5[15], and_9_out);  // OR_Gate
  buf or_9 (out_5[16], and_11_out);  // OR_Gate
  buf or_10 (out_5[17], and_10_out);  // OR_Gate
  buf or_11 (out_5[18], and_11_out);  // OR_Gate
  or or_12 (out_5[21], and_13_out, or_4_out, and_12_out);
  or or_13 (out_5[22], out_5[7], or_4_out);
  or or_14 (out_5[24], and_12_out, and_13_out);
  buf or_15 (out_5[27], and_11_out);  // OR_Gate

  assign {out_5[31:28], out_5[26:25], out_5[20:19], out_5[13], out_5[11:10], out_5[5:1]} = {{10{1'b0}}, out_5[23], out_5[8], out_5[9], out_5[6], 2'b00};

  // Notes on the sheet:
  //   110 = BEQ
  //   111 = BNE
  //   is my box currently selected
  //   get additional
  //   parameters from
  //   instruction
  //   STATUS FROM ALU
  //   falling edge check if the status was the same
  //   0 = BEQ, 1 = BNE
  //   if 2
  //   if 1
  //   if 3
  //   if 4
  //   if 5
  //   BNE
  //   BEQ
  //   if equal
  //   1 SAME FOR ALL
  //   2 SAME FOR ALL
  //   3 FOR BEQ
  //   3 FOR BNE
  //   AT THIS POINT THE PC CONTAINS THE CORRECT NEXT INSTRUCTION
  //   if the BNE/BEQ does not branch 
  //   then we must put PC+1 in PC
  //   ALU L TRANSMIT
  //   SUBTRACT
  //   if 1
  //   ALU R RECEIVE
  //   R1 TRANSMIT
  //   ALU R TRANSMIT
  //   PC A Read from IR
  //   IR TRANSMIT
  //   PC Read from PC A
  //   PC A Read from IR
  //   IR TRANSMIT
  //   PC Read from PC A
  //   ALU L RECEIVE
  //   R0 TRANSMIT
  //   if 2
  //   3
  //   4
  //   5
  //   6
  //   14
  //   0
  //   3
  //   8
  //   10
  //   18
  //   22
  //   25
endmodule

module _8bit__BCD (
  input  in_1,
  input  in_2,
  input  in_3,
  input  in_4,
  input  in_5,
  output out_6,
  output out_7,
  output out_8,
  output out_9,
  output out_10,
  output out_11,
  output out_12
);

  wire and_1_out, and_2_out, and_3_out, and_4_out, and_5_out, and_6_out, and_7_out, and_8_out, and_9_out,
       not_1_out, not_2_out, not_3_out, not_4_out, not_5_out, not_6_out, not_7_out, not_8_out, not_9_out,
       not_10_out, not_11_out, not_12_out, not_13_out, not_14_out, not_15_out, not_16_out, not_17_out,
       not_18_out, not_19_out, or_1_out, or_2_out, or_3_out, or_5_out, or_6_out, or_8_out, or_10_out,
       or_11_out, or_13_out, or_14_out, or_16_out, or_17_out, or_19_out, or_20_out, or_21_out, or_22_out,
       or_24_out, or_25_out;

  and and_1 (and_1_out, in_1, in_2);
  and and_2 (and_2_out, in_1, in_3);
  not not_1 (not_1_out, or_1_out);
  not not_2 (not_2_out, or_2_out);
  not not_3 (not_3_out, or_5_out);
  not not_4 (not_4_out, or_8_out);
  or or_1 (or_1_out, and_1_out, and_2_out, and_4_out, and_3_out);
  and and_3 (and_3_out, in_1, in_5);
  and and_4 (and_4_out, in_1, in_4);
  not not_5 (not_5_out, or_10_out);
  not not_6 (not_6_out, or_13_out);
  not not_7 (not_7_out, or_16_out);
  not not_8 (not_8_out, or_19_out);
  not not_9 (not_9_out, or_21_out);
  not not_10 (not_10_out, or_24_out);
  or or_2 (or_2_out, or_3_out, not_11_out);
  not not_11 (not_11_out, and_5_out);
  and and_5 (and_5_out, and_1_out, and_3_out);
  or or_3 (or_3_out, and_2_out, and_4_out);
  or or_4 (out_7, not_7_out, not_6_out, not_5_out, not_3_out, not_2_out, not_1_out);
  or or_5 (or_5_out, or_6_out, not_12_out);
  not not_12 (not_12_out, and_1_out);
  or or_6 (or_6_out, and_2_out, and_4_out, and_3_out);
  or or_7 (out_6, not_9_out, not_8_out, not_7_out, not_6_out, not_5_out, not_3_out, not_2_out);
  or or_8 (or_8_out, not_13_out, and_1_out);
  not not_13 (not_13_out, and_6_out);
  and and_6 (and_6_out, and_2_out, and_4_out, and_3_out);
  or or_9 (out_10, not_9_out, not_5_out, not_3_out, not_1_out);
  or or_10 (or_10_out, not_14_out, or_11_out);
  not not_14 (not_14_out, and_7_out);
  or or_11 (or_11_out, and_1_out, and_3_out);
  and and_7 (and_7_out, and_2_out, and_4_out);
  or or_12 (out_11, not_9_out, not_8_out, not_6_out, not_5_out, not_3_out, not_2_out, not_1_out);
  or or_13 (or_13_out, not_15_out, or_14_out);
  not not_15 (not_15_out, and_8_out);
  or or_14 (or_14_out, and_1_out, and_4_out);
  and and_8 (and_8_out, and_2_out, and_3_out);
  or or_15 (out_12, not_10_out, not_8_out, not_7_out, not_6_out, not_5_out, not_4_out, not_3_out, not_2_out, not_1_out);
  or or_16 (or_16_out, or_17_out, not_16_out);
  not not_16 (not_16_out, and_2_out);
  or or_17 (or_17_out, and_1_out, and_4_out, and_3_out);
  or or_18 (out_9, not_10_out, not_9_out, not_8_out, not_7_out, not_4_out, not_3_out, not_2_out, not_1_out);
  or or_19 (or_19_out, or_20_out, not_17_out);
  not not_17 (not_17_out, and_9_out);
  and and_9 (and_9_out, and_4_out, and_3_out);
  or or_20 (or_20_out, and_1_out, and_2_out);
  or or_21 (or_21_out, or_22_out, not_18_out);
  not not_18 (not_18_out, and_4_out);
  or or_22 (or_22_out, and_1_out, and_2_out, and_3_out);
  or or_23 (out_8, not_1_out, not_2_out, not_3_out, not_4_out, not_5_out, not_6_out, not_8_out, not_9_out);
  or or_24 (or_24_out, or_25_out, not_19_out);
  not not_19 (not_19_out, and_3_out);
  or or_25 (or_25_out, and_1_out, and_2_out, and_4_out);
endmodule

module Add_3 (
  input  in_1,
  input  in_2,
  input  in_3,
  input  in_4,
  output out_5,
  output out_6,
  output out_7,
  output out_8
);

  wire not_1_out, not_2_out, not_3_out, not_4_out, not_5_out, not_6_out, not_7_out, not_8_out, not_9_out,
       not_10_out, not_11_out, not_12_out, not_13_out, not_14_out, not_15_out, not_16_out, not_17_out,
       not_18_out, not_19_out, not_20_out, not_21_out, not_22_out, not_23_out, not_24_out, not_25_out;
  wire [1:0] not_50_out;
  wire [2:0] not_43_out, not_47_out;
  wire [2:1] not_45_out;
  wire [2:2] not_48_out;
  wire [3:0] and_11_out, and_12_out, and_13_out, and_14_out, and_15_out, and_16_out, and_17_out, and_18_out,
       and_19_out, and_20_out, not_29_out, not_35_out, not_40_out;
  wire [3:1] not_32_out;
  wire [3:2] not_37_out;
  wire [3:3] and_1_out, and_2_out, and_3_out, and_4_out, and_6_out, and_7_out, and_8_out, and_9_out,
       and_10_out;

  not not_1 (not_1_out, in_1);
  not not_2 (not_2_out, in_2);
  and and_1 (and_1_out[3], not_1_out, not_2_out, not_3_out, not_4_out);
  not not_3 (not_3_out, in_3);
  not not_4 (not_4_out, in_4);
  not not_5 (not_5_out, in_1);
  not not_6 (not_6_out, in_2);
  and and_2 (and_2_out[3], not_5_out, not_6_out, not_7_out, in_4);
  not not_7 (not_7_out, in_3);
  not not_8 (not_8_out, in_1);
  not not_9 (not_9_out, in_2);
  and and_3 (and_3_out[3], not_8_out, not_9_out, in_3, not_10_out);
  not not_10 (not_10_out, in_4);
  not not_11 (not_11_out, in_1);
  not not_12 (not_12_out, in_2);
  and and_4 (and_4_out[3], not_11_out, not_12_out, in_3, in_4);
  not not_13 (not_13_out, in_1);
  and and_5 (not_40_out[2], not_13_out, in_2, not_14_out, not_15_out);
  not not_14 (not_14_out, in_3);
  not not_15 (not_15_out, in_4);
  not not_16 (not_16_out, in_1);
  and and_6 (and_6_out[3], not_16_out, in_2, not_17_out, in_4);
  not not_17 (not_17_out, in_3);
  not not_18 (not_18_out, in_1);
  and and_7 (and_7_out[3], not_18_out, in_2, in_3, not_19_out);
  not not_19 (not_19_out, in_4);
  not not_20 (not_20_out, in_1);
  and and_8 (and_8_out[3], not_20_out, in_2, in_3, in_4);
  not not_21 (not_21_out, in_2);
  and and_9 (and_9_out[3], in_1, not_21_out, not_22_out, not_23_out);
  not not_22 (not_22_out, in_3);
  not not_23 (not_23_out, in_4);
  not not_24 (not_24_out, in_2);
  and and_10 (and_10_out[3], in_1, not_24_out, not_25_out, in_4);
  not not_25 (not_25_out, in_3);
  not not_26 (not_29_out[3], and_1_out[3]);
  not not_27 (not_29_out[2], and_1_out[3]);
  not not_28 (not_29_out[1], and_1_out[3]);
  not not_29 (not_29_out[0], and_1_out[3]);
  not not_30 (not_32_out[3], and_2_out[3]);
  not not_31 (not_32_out[2], and_2_out[3]);
  not not_32 (not_32_out[1], and_2_out[3]);
  not not_33 (not_35_out[3], and_3_out[3]);
  not not_34 (not_35_out[2], and_3_out[3]);
  not not_35 (not_35_out[0], and_3_out[3]);
  not not_36 (not_37_out[3], and_4_out[3]);
  not not_37 (not_37_out[2], and_4_out[3]);
  not not_38 (not_40_out[3], not_40_out[2]);
  not not_39 (not_40_out[1], not_40_out[2]);
  not not_40 (not_40_out[0], not_40_out[2]);
  not not_41 (not_43_out[2], and_6_out[3]);
  not not_42 (not_43_out[1], and_6_out[3]);
  not not_43 (not_43_out[0], and_6_out[3]);
  not not_44 (not_45_out[2], and_7_out[3]);
  not not_45 (not_45_out[1], and_7_out[3]);
  not not_46 (not_47_out[2], and_8_out[3]);
  not not_47 (not_47_out[0], and_8_out[3]);
  not not_48 (not_48_out[2], and_9_out[3]);
  not not_49 (not_50_out[1], and_10_out[3]);
  not not_50 (not_50_out[0], and_10_out[3]);
  assign and_11_out = {4{not_40_out[2]}} & not_40_out;  // AND_Gate and_11, 4 bits wide
  assign and_12_out = {4{and_6_out[3]}} & {and_6_out[3], not_43_out};  // AND_Gate and_12, 4 bits wide
  assign and_13_out = {4{and_7_out[3]}} & {and_7_out[3], not_45_out, and_7_out[3]};  // AND_Gate and_13, 4 bits wide
  assign and_14_out = {4{and_8_out[3]}} & {and_8_out[3], not_47_out[2], and_8_out[3], not_47_out[0]};  // AND_Gate and_14, 4 bits wide
  assign and_15_out = {4{and_9_out[3]}} & {and_9_out[3], not_48_out[2], {2{and_9_out[3]}}};  // AND_Gate and_15, 4 bits wide
  assign and_16_out = {4{and_10_out[3]}} & {{2{and_10_out[3]}}, not_50_out};  // AND_Gate and_16, 4 bits wide
  assign and_17_out = {4{and_1_out[3]}} & not_29_out;  // AND_Gate and_17, 4 bits wide
  assign and_18_out = {4{and_2_out[3]}} & {not_32_out, and_2_out[3]};  // AND_Gate and_18, 4 bits wide
  assign and_19_out = {4{and_3_out[3]}} & {not_35_out[3:2], and_3_out[3], not_35_out[0]};  // AND_Gate and_19, 4 bits wide
  assign and_20_out = {4{and_4_out[3]}} & {not_37_out, {2{and_4_out[3]}}};  // AND_Gate and_20, 4 bits wide
  assign {out_5, out_6, out_7, out_8} = and_17_out | and_18_out | and_19_out | and_20_out | and_11_out | and_12_out | and_13_out | and_14_out | and_15_out | and_16_out;  // OR_Gate or_1, 4 bits wide
endmodule

module _8bit__display (
  input  in_1,
  input  in_2,
  input  in_3,
  input  in_4,
  input  in_5,
  input  in_6,
  input  in_7,
  input  in_8,
  output out_9,
  output out_10,
  output out_11,
  output out_12,
  output out_13,
  output out_14,
  output out_15,
  output out_16,
  output out_17,
  output out_18,
  output out_19,
  output out_20
);

  wire add_3_1_out_5, add_3_1_out_6, add_3_1_out_7, add_3_1_out_8, add_3_2_out_5, add_3_2_out_6,
       add_3_2_out_7, add_3_2_out_8, add_3_3_out_5, add_3_3_out_6, add_3_3_out_7, add_3_3_out_8,
       add_3_4_out_5, add_3_4_out_6, add_3_4_out_7, add_3_4_out_8, add_3_5_out_6, add_3_5_out_7,
       add_3_5_out_8;

  Add_3 add_3_1 (
    .out_5(add_3_1_out_5), .out_6(add_3_1_out_6), .in_1(1'b0), .out_7(add_3_1_out_7), .out_8(add_3_1_out_8),
    .in_2(in_1), .in_3(in_2), .in_4(in_3));
  Add_3 add_3_2 (
    .out_5(add_3_2_out_5), .out_6(add_3_2_out_6), .in_1(add_3_1_out_6), .out_7(add_3_2_out_7),
    .out_8(add_3_2_out_8), .in_2(add_3_1_out_7), .in_3(add_3_1_out_8), .in_4(in_4));
  Add_3 add_3_3 (
    .out_5(add_3_3_out_5), .out_6(add_3_3_out_6), .in_1(add_3_2_out_6), .out_7(add_3_3_out_7),
    .out_8(add_3_3_out_8), .in_2(add_3_2_out_7), .in_3(add_3_2_out_8), .in_4(in_5));
  Add_3 add_3_4 (
    .out_5(add_3_4_out_5), .out_6(add_3_4_out_6), .in_1(add_3_3_out_6), .out_7(add_3_4_out_7),
    .out_8(add_3_4_out_8), .in_2(add_3_3_out_7), .in_3(add_3_3_out_8), .in_4(in_6));
  Add_3 add_3_5 (
    .out_5(out_11), .out_6(add_3_5_out_6), .in_1(1'b0), .out_7(add_3_5_out_7), .out_8(add_3_5_out_8),
    .in_2(add_3_1_out_5), .in_3(add_3_2_out_5), .in_4(add_3_3_out_5));
  Add_3 add_3_6 (
    .out_5(out_12), .out_6(out_13), .in_1(add_3_5_out_6), .out_7(out_14), .out_8(out_15),
    .in_2(add_3_5_out_7), .in_3(add_3_5_out_8), .in_4(add_3_4_out_5));
  Add_3 add_3_7 (
    .out_5(out_16), .out_6(out_17), .in_1(add_3_4_out_6), .out_7(out_18), .out_8(out_19),
    .in_2(add_3_4_out_7), .in_3(add_3_4_out_8), .in_4(in_7));

  assign out_9 = 1'b0;
  assign out_10 = 1'b0;
  assign out_20 = in_8;
endmodule

module BCD__screen (
  input  in_1,
  input  [7:0] in_2,
  output out_3,
  output out_4,
  output out_5,
  output out_6,
  output out_7,
  output out_8,
  output out_9,
  output out_10,
  output out_11,
  output out_12,
  output out_13,
  output out_14,
  output out_15,
  output out_16,
  output out_17,
  output out_18,
  output out_19,
  output out_20,
  output out_21,
  output out_22,
  output out_23
);

  wire n8bit_display_1_out_9, n8bit_display_1_out_10, n8bit_display_1_out_11, n8bit_display_1_out_12,
       n8bit_display_1_out_13, n8bit_display_1_out_14, n8bit_display_1_out_15, n8bit_display_1_out_16,
       n8bit_display_1_out_17, n8bit_display_1_out_18, n8bit_display_1_out_19, n8bit_display_1_out_20;

  _8bit__display u_8bit_display_1 (
    .in_1(in_2[7]), .in_2(in_2[6]), .in_3(in_2[5]), .in_4(in_2[4]), .in_5(in_2[3]), .in_6(in_2[2]),
    .in_7(in_2[1]), .in_8(in_2[0]), .out_9(n8bit_display_1_out_9), .out_10(n8bit_display_1_out_10),
    .out_11(n8bit_display_1_out_11), .out_12(n8bit_display_1_out_12), .out_13(n8bit_display_1_out_13),
    .out_14(n8bit_display_1_out_14), .out_15(n8bit_display_1_out_15), .out_16(n8bit_display_1_out_16),
    .out_17(n8bit_display_1_out_17), .out_18(n8bit_display_1_out_18), .out_19(n8bit_display_1_out_19),
    .out_20(n8bit_display_1_out_20));
  _8bit__BCD u_8bit_bcd_1 (
    .out_10(out_15), .out_11(out_16), .out_12(out_17), .in_2(n8bit_display_1_out_9),
    .in_3(n8bit_display_1_out_10), .in_4(n8bit_display_1_out_11), .in_5(n8bit_display_1_out_12),
    .out_6(out_3), .out_7(out_4), .out_8(out_5), .out_9(out_6), .in_1(in_1));
  _8bit__BCD u_8bit_bcd_2 (
    .out_10(out_18), .out_11(out_19), .out_12(out_20), .in_2(n8bit_display_1_out_13),
    .in_3(n8bit_display_1_out_14), .in_4(n8bit_display_1_out_15), .in_5(n8bit_display_1_out_16),
    .out_6(out_7), .out_7(out_8), .out_8(out_9), .out_9(out_10), .in_1(in_1));
  _8bit__BCD u_8bit_bcd_3 (
    .out_10(out_21), .out_11(out_22), .out_12(out_23), .in_2(n8bit_display_1_out_17),
    .in_3(n8bit_display_1_out_18), .in_4(n8bit_display_1_out_19), .in_5(n8bit_display_1_out_20),
    .out_6(out_11), .out_7(out_12), .out_8(out_13), .out_9(out_14), .in_1(in_1));
endmodule

module ROM (
  input  in_1,
  output receive,
  output Transmit,
  output [7:0] out_4,
  output [7:0] out_5,
  output out_6,
  output receive_2,
  output Transmit_2,
  output out_9
);

  wire and_2_out, and_4_out, and_6_out, clock_1_out, d_ff_1_q, d_ff_2_q, j_k_ff_1_q, j_k_ff_1_qn,
       n2_8_1_1_out_3, n2_8_1_2_out_3, n2_8_1_3_out_3, n2_8_1_4_out_3, n2_8_1_5_out_3, n2_8_1_6_out_3,
       n2_8_1_7_out_3, n2_8_1_8_out_3, n2_8_1_9_out_3, n2_8_1_10_out_3, n2_8_1_11_out_3, n2_8_1_12_out_3,
       n2_8_1_13_out_3, n2_8_1_14_out_3, n2_8_1_15_out_3, n2_8_1_16_out_3, n2_8_1_17_out_3, not_1_out,
       not_3_out, not_4_out, not_5_out, not_7_out, or_1_out;
  wire [7:0] adder_1_out_2, n1_1_8_1_out_3, register_1_out_5, register_2_out_5, register_3_out_5,
       register_4_out_5, register_5_out_5, register_6_out_5, register_7_out_5, register_8_out_5,
       register_9_out_5, register_10_out_5, register_11_out_5, register_12_out_5, register_13_out_5,
       register_14_out_5, register_15_out_5, register_16_out_5, register_17_out_5;

  Clock clock_1 (.out(clock_1_out));
  not not_1 (not_1_out, in_1);
  D_Flip_Flop d_ff_1 (
    .clk(clock_1_out), .D(not_3_out), .Q(d_ff_1_q), .preset(not_1_out), .reset(j_k_ff_1_q));  // open: Qn, en
  D_Flip_Flop d_ff_2 (
    .clk(d_ff_1_q), .D(not_4_out), .Q(d_ff_2_q), .preset(not_1_out), .reset(j_k_ff_1_q));  // open: Qn, en
  _2_8__1 u_2_8_1_1 (.in_1(register_1_out_5), .in_2(8'h10), .out_3(n2_8_1_1_out_3));
  not not_2 (out_6, not_1_out);
  not not_3 (not_3_out, d_ff_1_q);
  not not_4 (not_4_out, d_ff_2_q);
  J_K_Flip_Flop j_k_ff_1 (
    .J(n2_8_1_1_out_3), .clk(clock_1_out), .K(1'b0), .Q(j_k_ff_1_q), .Qn(j_k_ff_1_qn));  // open: preset, en, reset
  not not_5 (not_5_out, not_3_out);
  not not_6 (out_9, j_k_ff_1_qn);
  not not_7 (not_7_out, not_4_out);
  and and_1 (Transmit, not_4_out, not_5_out);
  and and_2 (and_2_out, not_4_out, not_3_out);
  _1_1__8 u_1_1_8_1 (.in_1(out_6), .out_3(n1_1_8_1_out_3), .in_2(out_6));
  and and_3 (receive, not_3_out, not_7_out);
  and and_4 (and_4_out, and_2_out, j_k_ff_1_qn);
  or or_1 (or_1_out, receive, and_4_out);
  register register_1 (
    .in_2(or_1_out), .in_4(adder_1_out_2), .out_5(register_1_out_5), .enable_receiving(and_4_out),
    .ON_OFF(in_1));
  assign out_4 = n1_1_8_1_out_3 & register_1_out_5;  // AND_Gate and_5, 8 bits wide
  Adder adder_1 (.in_1(register_1_out_5), .out_2(adder_1_out_2));  // open: out_3
  _2_8__1 u_2_8_1_2 (.in_1(register_1_out_5), .in_2({8{1'b0}}), .out_3(n2_8_1_2_out_3));
  _2_8__1 u_2_8_1_3 (.in_1(register_1_out_5), .in_2(8'h1), .out_3(n2_8_1_3_out_3));
  _2_8__1 u_2_8_1_4 (.in_1(register_1_out_5), .in_2(8'h2), .out_3(n2_8_1_4_out_3));
  _2_8__1 u_2_8_1_5 (.in_1(register_1_out_5), .in_2(8'h3), .out_3(n2_8_1_5_out_3));
  _2_8__1 u_2_8_1_6 (.in_1(register_1_out_5), .in_2(8'h4), .out_3(n2_8_1_6_out_3));
  _2_8__1 u_2_8_1_7 (.in_1(register_1_out_5), .in_2(8'h5), .out_3(n2_8_1_7_out_3));
  _2_8__1 u_2_8_1_8 (.in_1(register_1_out_5), .in_2(8'h6), .out_3(n2_8_1_8_out_3));
  _2_8__1 u_2_8_1_9 (.in_1(register_1_out_5), .in_2(8'h7), .out_3(n2_8_1_9_out_3));
  _2_8__1 u_2_8_1_10 (.in_1(register_1_out_5), .in_2(8'h8), .out_3(n2_8_1_10_out_3));
  _2_8__1 u_2_8_1_11 (.in_1(register_1_out_5), .in_2(8'h9), .out_3(n2_8_1_11_out_3));
  _2_8__1 u_2_8_1_12 (.in_1(register_1_out_5), .in_2(8'ha), .out_3(n2_8_1_12_out_3));
  _2_8__1 u_2_8_1_13 (.in_1(register_1_out_5), .in_2(8'hb), .out_3(n2_8_1_13_out_3));
  _2_8__1 u_2_8_1_14 (.in_1(register_1_out_5), .in_2(8'hc), .out_3(n2_8_1_14_out_3));
  _2_8__1 u_2_8_1_15 (.in_1(register_1_out_5), .in_2(8'hd), .out_3(n2_8_1_15_out_3));
  _2_8__1 u_2_8_1_16 (.in_1(register_1_out_5), .in_2(8'he), .out_3(n2_8_1_16_out_3));
  _2_8__1 u_2_8_1_17 (.in_1(register_1_out_5), .in_2(8'hf), .out_3(n2_8_1_17_out_3));
  and and_6 (and_6_out, in_1, n2_8_1_2_out_3);
  register register_2 (
    .in_2(and_6_out), .in_4(8'h4c), .out_5(register_2_out_5), .ON_OFF(in_1));  // open: enable_receiving
  register register_3 (
    .in_2(n2_8_1_3_out_3), .in_4(8'h80), .out_5(register_3_out_5), .ON_OFF(in_1));  // open: enable_receiving
  register register_4 (
    .in_2(n2_8_1_4_out_3), .in_4(8'h6d), .out_5(register_4_out_5), .ON_OFF(in_1));  // open: enable_receiving
  register register_5 (
    .in_2(n2_8_1_5_out_3), .in_4(8'h4e), .out_5(register_5_out_5), .ON_OFF(in_1));  // open: enable_receiving
  register register_6 (
    .in_2(n2_8_1_6_out_3), .in_4(8'h5f), .out_5(register_6_out_5), .ON_OFF(in_1));  // open: enable_receiving
  register register_7 (
    .in_2(n2_8_1_7_out_3), .in_4(8'h80), .out_5(register_7_out_5), .ON_OFF(in_1));  // open: enable_receiving
  register register_8 (
    .in_2(n2_8_1_8_out_3), .in_4(8'h6e), .out_5(register_8_out_5), .ON_OFF(in_1));  // open: enable_receiving
  register register_9 (
    .in_2(n2_8_1_9_out_3), .in_4(8'h5d), .out_5(register_9_out_5), .ON_OFF(in_1));  // open: enable_receiving
  register register_10 (
    .in_2(n2_8_1_10_out_3), .in_4(8'ha0), .out_5(register_10_out_5), .ON_OFF(in_1));  // open: enable_receiving
  register register_11 (
    .in_2(n2_8_1_11_out_3), .in_4(8'he0), .out_5(register_11_out_5), .ON_OFF(in_1));  // open: enable_receiving
  register register_12 (
    .in_2(n2_8_1_12_out_3), .in_4(8'h4e), .out_5(register_12_out_5), .ON_OFF(in_1));  // open: enable_receiving
  register register_13 (
    .in_2(n2_8_1_13_out_3), .in_4(8'hb0), .out_5(register_13_out_5), .ON_OFF(in_1));  // open: enable_receiving
  register register_14 (
    .in_2(n2_8_1_14_out_3), .in_4(8'h1), .out_5(register_14_out_5), .ON_OFF(in_1));  // open: enable_receiving
  register register_15 (
    .in_2(n2_8_1_15_out_3), .in_4({8{1'b0}}), .out_5(register_15_out_5), .ON_OFF(in_1));  // open: enable_receiving
  register register_16 (
    .in_2(n2_8_1_16_out_3), .in_4({8{1'b0}}), .out_5(register_16_out_5), .ON_OFF(in_1));  // open: enable_receiving
  register register_17 (
    .in_2(n2_8_1_17_out_3), .in_4(8'h9), .out_5(register_17_out_5), .ON_OFF(in_1));  // open: enable_receiving
  assign out_5 = register_2_out_5 | register_3_out_5 | register_4_out_5 | register_5_out_5 | register_6_out_5 | register_7_out_5 | register_8_out_5 | register_9_out_5 | register_10_out_5 | register_11_out_5 | register_12_out_5 | register_13_out_5 | register_14_out_5 | register_15_out_5 | register_16_out_5 | register_17_out_5;  // OR_Gate or_2, 8 bits wide

  assign receive_2 = receive;
  assign Transmit_2 = Transmit;

  // Notes on the sheet:
  //   Write Mode
  //   Address
  //   Data
endmodule

module Input_Buffer (
  input  Buffer_Transmit,
  input  ON_OFF,
  input  [9:0] in_3,
  output [7:0] out_4
);

  wire [3:0] or_1_out;

  or or_1 (or_1_out[0], in_3[1], in_3[3], in_3[5], in_3[7], in_3[9]);
  or or_2 (or_1_out[1], in_3[2], in_3[3], in_3[6], in_3[7]);
  or or_3 (or_1_out[2], in_3[7], in_3[6], in_3[5], in_3[4]);
  or or_4 (or_1_out[3], in_3[8], in_3[9]);
  register register_1 (
    .in_2(Buffer_Transmit), .in_4({4'b0000, or_1_out}), .out_5(out_4), .enable_receiving(1'b1),
    .ON_OFF(ON_OFF));

  // Notes on the sheet:
  //   1
  //   2
  //   3
  //   4
  //   5
  //   6
  //   7
  //   8
  //   9
endmodule

module Init_CPU (
  input  in_1,
  output [31:0] out_2
);

  wire and_1_out, and_2_out, and_3_out, and_9_out, clock_1_out, clock_2_out, d_ff_1_qn, d_ff_2_qn, d_ff_3_q,
       d_ff_4_q, d_ff_5_q, not_1_out, not_2_out, not_3_out, not_4_out, not_5_out, not_6_out, not_7_out,
       not_8_out, not_9_out, not_10_out, not_11_out, not_12_out, not_13_out, not_14_out, or_1_out;

  and and_1 (and_1_out, in_1, d_ff_2_qn);
  not not_1 (not_1_out, in_1);
  Clock clock_1 (.out(clock_1_out));
  or or_1 (or_1_out, and_3_out, and_2_out);
  and and_2 (and_2_out, clock_1_out, in_1, and_9_out);
  and and_3 (and_3_out, clock_1_out, not_1_out);
  D_Flip_Flop d_ff_1 (.clk(clock_1_out), .D(and_1_out), .Qn(d_ff_1_qn));  // open: Q, preset, en, reset
  D_Flip_Flop d_ff_2 (.clk(or_1_out), .D(in_1), .Qn(d_ff_2_qn));  // open: Q, preset, en, reset
  Clock clock_2 (.out(clock_2_out));
  D_Flip_Flop d_ff_3 (.clk(clock_2_out), .D(not_2_out), .Q(d_ff_3_q), .preset(d_ff_1_qn));  // open: Qn, en, reset
  D_Flip_Flop d_ff_4 (.clk(d_ff_3_q), .D(not_3_out), .Q(d_ff_4_q), .preset(d_ff_1_qn));  // open: Qn, en, reset
  D_Flip_Flop d_ff_5 (.clk(d_ff_4_q), .D(not_4_out), .Q(d_ff_5_q), .preset(d_ff_1_qn));  // open: Qn, en, reset
  not not_2 (not_2_out, d_ff_3_q);
  not not_3 (not_3_out, d_ff_4_q);
  not not_4 (not_4_out, d_ff_5_q);
  not not_5 (not_5_out, d_ff_1_qn);
  not not_6 (not_6_out, not_3_out);
  not not_7 (not_7_out, not_4_out);
  not not_8 (not_8_out, not_2_out);
  not not_9 (not_9_out, not_4_out);
  not not_10 (not_10_out, not_4_out);
  not not_11 (not_11_out, not_2_out);
  not not_12 (not_12_out, not_3_out);
  not not_13 (not_13_out, not_3_out);
  not not_14 (not_14_out, not_2_out);
  and and_4 (out_2[7], not_2_out, not_6_out, not_7_out);
  and and_5 (out_2[8], not_8_out, not_3_out, not_9_out);
  and and_6 (out_2[6], not_2_out, not_3_out, not_10_out);
  and and_7 (out_2[9], not_11_out, not_12_out, not_4_out);
  and and_8 (out_2[23], not_2_out, not_13_out, not_4_out);
  and and_9 (and_9_out, not_14_out, not_3_out, not_4_out);
  buf or_2 (out_2[0], 1'b0);  // OR_Gate
  buf or_3 (out_2[12], 1'b0);  // OR_Gate
  buf or_4 (out_2[14], 1'b0);  // OR_Gate
  buf or_5 (out_2[15], 1'b0);  // OR_Gate
  buf or_6 (out_2[16], 1'b0);  // OR_Gate
  buf or_7 (out_2[17], 1'b0);  // OR_Gate
  buf or_8 (out_2[18], 1'b0);  // OR_Gate
  buf or_9 (out_2[21], 1'b0);  // OR_Gate
  buf or_10 (out_2[22], out_2[7]);  // OR_Gate
  buf or_11 (out_2[24], 1'b0);  // OR_Gate
  buf or_12 (out_2[27], 1'b0);  // OR_Gate

  assign {out_2[31:28], out_2[26:25], out_2[20:19], out_2[13], out_2[11:10], out_2[5:1]} = {{10{1'b0}}, out_2[23], out_2[8], out_2[9], out_2[6], 2'b00};

  // Notes on the sheet:
  //   if 1
  //   if 2
  //   3
  //   4
  //   5
  //   6
  //   14
  //   0
  //   3
  //   8
  //   10
  //   18
  //   22
  //   25
endmodule
